// Logisim project alu.circ as structural Verilog: 1 circuit, main circuit alu
module alu (
  input  [31:0] A,
  input  [31:0] B,
  input  [3:0] ALUSel,
  output [31:0] Result
);

  wire [31:0] adder_1_out, and_1_out, comparator_1_lt, divider_2_rem, multiplier_1_out, multiplier_2_out,
       or_1_out, shifter_1_out, shifter_2_out, shifter_3_out, subtractor_1_out, undriven, xor_1_out;

  Adder #(.width(32)) adder_1 (.a(A), .b(B), .out(adder_1_out));  // open: cin, cout
  assign and_1_out = A & B;  // AND_Gate and_1, 32 bits wide
  assign or_1_out = A | B;  // OR_Gate or_1, 32 bits wide
  assign xor_1_out = A ^ B;  // XOR_Gate xor_1, 32 bits wide
  Shifter #(.width(32), .shift("lr")) shifter_1 (.in(A), .out(shifter_1_out));  // open: dist
  Shifter #(.width(32), .shift("ar")) shifter_2 (.in(A), .out(shifter_2_out));  // open: dist
  Shifter #(.width(32)) shifter_3 (.in(A), .out(shifter_3_out));  // open: dist
  Comparator #(.width(32)) comparator_1 (.a(A), .b(B), .lt(comparator_1_lt[0]));  // open: gt, eq
  Divider #(.width(32)) divider_1 (.a(B), .b(A), .upper(undriven));  // open: out, rem
  Divider #(.width(32)) divider_2 (.a(B), .b(A), .rem(divider_2_rem));  // open: out, upper
  Multiplier #(.width(32)) multiplier_1 (.a(B), .b(A), .out(multiplier_1_out));  // open: cin, cout
  Multiplier #(.width(32)) multiplier_2 (.a(A), .b(B), .out(multiplier_2_out));  // open: cin, cout
  Subtractor #(.width(32)) subtractor_1 (.a(B), .b(A), .out(subtractor_1_out));  // open: bin, bout
  Multiplexer #(.enable("false")) multiplexer_1 ();  // open: in0, in1, out, sel
  Multiplexer #(.select(4), .width(32), .enable("false")) multiplexer_2 (
    .in0(adder_1_out), .in1(and_1_out), .in2(or_1_out), .in3(xor_1_out), .in4(shifter_1_out),
    .in5(shifter_2_out), .in6(shifter_3_out), .in7(comparator_1_lt), .in8(undriven), .in9(divider_2_rem),
    .in10(multiplier_1_out), .in11(multiplier_2_out), .in12(subtractor_1_out));  // open: in13, in14, in15, out, sel
  // Pins of 1 and 32 bits meet at comparator_1_lt

  // Notes on the sheet:
  //   INPUTS to your circuit
  //   add
  //   and
  //   or
  //   xor
  //   srl
  //   sra
  //   sll
  //   slt
  //   divu
  //   remu
  //   mul
  //   mulhu
  //   sub
  //   bsel
  //   DON'T CHANGE THE LOCATIONS OF THE INPUTS AND OUTPUTS!
  //   OUTPUT from your circuit
endmodule
