// Logisim project cpu.circ as structural Verilog: 4 circuits, main circuit main
module main (
  input  [31:0] INSTRUCTION,
  input  CLOCK,
  output [31:0] PROGRAM_COUNTER,
  output [31:0] ra,
  output [31:0] sp,
  output [31:0] t0,
  output [31:0] t1,
  output [31:0] t2,
  output [31:0] s0,
  output [31:0] s1,
  output [31:0] a0
);

  wire ASel, BrEq, BrLt, BrUn, BSel, DMEM_p1, DMEM_p5, MemRW, PCSel, RegWEn;
  wire [1:0] WBSel;
  wire [2:0] ImmSel;
  wire [3:0] ALUSel;
  wire [6:0] INSTRUCTION_OUT;
  wire [24:0] imm;
  wire [31:0] ALU_Out, DMEM_out, imm_Extended, multiplexer_1_out, multiplexer_2_out, multiplexer_3_out, PC4,
       rs1_Out, rs2_Out, wb;

  Multiplexer #(.width(32), .enable("false")) multiplexer_1 (
    .in0(PC4), .in1(ALU_Out), .out(multiplexer_1_out), .sel(PCSel));
  Register #(.width(32)) PC (.D(multiplexer_1_out), .clk(CLOCK), .Q(PROGRAM_COUNTER));  // open: en, clr
  Register #(.width(32)) register_1 (.D(INSTRUCTION), .clk(CLOCK), .Q({imm, INSTRUCTION_OUT}));  // open: en, clr
  Adder #(.width(32)) adder_1 (.a(PROGRAM_COUNTER), .b(32'h4), .out(PC4));  // open: cin, cout
  immGen immgen_1 (.imm_Out(imm_Extended), .inst_In(imm), .immSel(ImmSel));
  regfile_main RegFile (
    .rs2(imm[17:13]), .rd(imm[4:0]), .Read_Data_1(rs1_Out), .Read_Data_2(rs2_Out), .ra(ra), .sp(sp), .t0(t0),
    .t1(t1), .t2(t2), .s0(s0), .s1(s1), .a0(a0), .rs1(imm[12:8]), .Write_Data(wb), .RegWEn(RegWEn),
    .clk(CLOCK));
  branchComp branchcomp_1 (.rs1(rs1_Out), .rs2(rs2_Out), .BrUn(BrUn), .BrLt(BrLt), .BrEq(BrEq));
  Multiplexer #(.width(32), .enable("false")) multiplexer_2 (
    .in0(rs1_Out), .in1(PROGRAM_COUNTER), .out(multiplexer_2_out), .sel(ASel));
  Multiplexer #(.width(32), .enable("false")) multiplexer_3 (
    .in0(rs2_Out), .in1(imm_Extended), .out(multiplexer_3_out), .sel(BSel));
  alu Arithmetic_Logic_Unit (.Result(ALU_Out), .ALUSel(ALUSel), .A(multiplexer_2_out), .B(multiplexer_3_out));
  control control_1 (
    .inst_in({imm, INSTRUCTION_OUT}), .BrLt(BrLt), .BrEq(BrEq), .PCSel(PCSel), .RegWEn(RegWEn),
    .ImmSel(ImmSel), .BrUn(BrUn), .ASel(ASel), .BSel(BSel), .ALUSel(ALUSel), .MemRW(MemRW), .WBSel(WBSel));  // open: out_13
  // mem_main DMEM: pin names not known; wires that end beside it: DMEM_p1, DMEM_p1, ALU_Out, rs2_Out, DMEM_p5, CLOCK, MemRW, DMEM_out
  Multiplexer #(.select(2), .width(32), .enable("false")) multiplexer_4 (
    .in0(PC4), .in1(ALU_Out), .in2(DMEM_out), .out(wb), .sel(WBSel));  // open: in3

  // Other names for the same wires on the sheet: clk = CLOCK; INSTRUCTION_OUT[31:7] = imm; rd[4:0] = imm[4:0];
  //   rs1_In[4:0] = imm[12:8]; rs2_In[4:0] = imm[17:13]

  // Notes on the sheet:
  //   Output
  //   IMEM (do **NOT** move this)
  //   Inputs
  //   Inputs/Outputs for testing. Do **NOT** move these.
endmodule

module immGen (
  input  [24:0] inst_In,
  input  [2:0] immSel,
  output [31:0] imm_Out
);

  wire [31:0] I, S, SB, UJ;

  assign I = {{20{inst_In[24]}}, inst_In[24:13]};  // Bit_Extender bit_extender_1
  assign S = {{20{inst_In[24]}}, {inst_In[24:18], inst_In[4:0]}};  // Bit_Extender bit_extender_2
  assign SB = {{19{inst_In[24]}}, {inst_In[24], inst_In[0], inst_In[23:18], inst_In[4:1], 1'b0}};  // Bit_Extender bit_extender_3
  assign UJ = {{11{inst_In[24]}}, {inst_In[24], inst_In[12:5], inst_In[13], inst_In[23:14], 1'b0}};  // Bit_Extender bit_extender_4
  Multiplexer #(.select(3), .width(32), .enable("false")) multiplexer_1 (
    .in0(I), .in1(S), .in2(SB), .in3({inst_In[24:5], {12{1'b0}}}), .in4(UJ), .out(imm_Out), .sel(immSel));  // open: in5, in6, in7

  // Other names for the same wires on the sheet: Instruction_In[24:0] = inst_In; U[31:12] = inst_In[24:5]
endmodule

module control (
  input  [31:0] inst_in,
  input  BrLt,
  input  BrEq,
  output PCSel,
  output RegWEn,
  output [2:0] ImmSel,
  output BrUn,
  output ASel,
  output BSel,
  output [3:0] ALUSel,
  output MemRW,
  output [1:0] WBSel,
  output [14:0] out_13
);

  ROM #(.addrWidth(12), .dataWidth(15)) rom_1 (
    .addr({inst_in[30], inst_in[25], inst_in[14:12], inst_in[6:2], BrEq, BrLt}),
    .data({out_13[14:13], ImmSel, BrUn, ASel, BSel, ALUSel, MemRW, out_13[1:0]}));

  assign out_13[12:2] = {ImmSel, BrUn, ASel, BSel, ALUSel, MemRW};
  assign PCSel = out_13[14];
  assign RegWEn = out_13[13];
  assign WBSel = out_13[1:0];

  // Other names for the same wires on the sheet: opcode[4:0] = inst_in[6:2]; func3[2:0] = inst_in[14:12];
  //   func7_0 = inst_in[25]; func7_1 = inst_in[30];
  //   controlword[14:0] = {out_13[14:13], ImmSel, BrUn, ASel, BSel, ALUSel, MemRW, out_13[1:0]}

  // Notes on the sheet:
  //   contents of rom_1 (hex, n*v repeats v):
  //   48*0 4*2001 124*0 4*2031 124*0 4*2039 252*0 4*2019 124*0 4*2021 124*0 4*2011 124*0 4*2009 124*0
  //   4*2051 124*0 4*2071 252*0 4*2059 252*0 4*2041 252*0 4*2049 124*0 4*2061
endmodule

module branchComp (
  input  [31:0] rs1,
  input  [31:0] rs2,
  input  BrUn,
  output BrLt,
  output BrEq
);

  wire BrEqSigned, BrEqUnsigned, BrLtSigned, BrLtUnsigned;

  Comparator #(.width(32)) comparator_1 (.a(rs1), .b(rs2), .eq(BrEqSigned), .lt(BrLtSigned));  // open: gt
  Comparator #(.width(32), .mode("unsigned")) comparator_2 (
    .a(rs1), .b(rs2), .eq(BrEqUnsigned), .lt(BrLtUnsigned));  // open: gt
  Multiplexer #(.enable("false")) multiplexer_1 (.in0(BrLtSigned), .in1(BrLtUnsigned), .out(BrLt), .sel(BrUn));
  Multiplexer #(.enable("false")) multiplexer_2 (.in0(BrEqSigned), .in1(BrEqUnsigned), .out(BrEq), .sel(BrUn));
endmodule
