// Logisim project alu.circ as structural Verilog: 1 circuit, main circuit alu
module alu (
  input  [31:0] A,
  input  [31:0] B,
  input  [3:0] ALUSel,
  output [31:0] Result
);

  wire slt0;
  wire [31:0] add0, and0, divu, mul, mulhu, or0, remu, sll0, sra0, srl0, sub0, xor0;

  Adder #(.width(32)) adder_1 (.a(A), .b(B), .out(add0));  // open: cin, cout
  assign and0 = A & B;  // AND_Gate and_1, 32 bits wide
  assign or0 = A | B;  // OR_Gate or_1, 32 bits wide
  assign xor0 = A ^ B;  // XOR_Gate xor_1, 32 bits wide
  Shifter #(.width(32), .shift("lr")) shifter_1 (.in(A), .\dist (B[4:0]), .out(srl0));
  Shifter #(.width(32), .shift("ar")) shifter_2 (.in(A), .\dist (B[4:0]), .out(sra0));
  Shifter #(.width(32)) shifter_3 (.in(A), .\dist (B[4:0]), .out(sll0));
  Comparator #(.width(32)) comparator_1 (.a(A), .b(B), .lt(slt0));  // open: gt, eq
  Divider #(.width(32)) divider_1 (.a(B), .b(A), .upper(divu));  // open: out, rem
  Divider #(.width(32)) divider_2 (.a(B), .b(A), .rem(remu));  // open: out, upper
  Multiplier #(.width(32)) multiplier_1 (.a(B), .b(A), .out(mul));  // open: cin, cout
  Multiplier #(.width(32)) multiplier_2 (.a(A), .b(B), .out(mulhu));  // open: cin, cout
  Subtractor #(.width(32)) subtractor_1 (.a(B), .b(A), .out(sub0));  // open: bin, bout
  Multiplexer #(.enable("false")) multiplexer_1 ();  // open: in0, in1, out, sel
  Multiplexer #(.select(4), .width(32), .enable("false")) multiplexer_2 (
    .in0(add0), .in1(and0), .in2(or0), .in3(xor0), .in4(srl0), .in5(sra0), .in6(sll0), .in8(divu),
    .in9(remu), .in10(mul), .in11(mulhu), .in12(sub0), .out(Result), .sel(ALUSel));  // open: in7, in13, in14, in15

  // Notes on the sheet:
  //   INPUTS to your circuit
  //   add
  //   and
  //   or
  //   xor
  //   srl
  //   sra
  //   sll
  //   slt
  //   divu
  //   remu
  //   mul
  //   mulhu
  //   sub
  //   bsel
  //   DON'T CHANGE THE LOCATIONS OF THE INPUTS AND OUTPUTS!
  //   OUTPUT from your circuit
endmodule
